# Fritzing sketch Controller (saved by Fritzing 0.9.1b)

parts:
  Part1 = Arduino Uno (Rev3)  # not connected
  Part2 = Adafruit Proto Shield for Arduino Kit - v.5
  Part3 = Bluetooth HC-05 Macho
  JP2 = Header 1 [package=1x01_offset]  # not connected
  JP3 = Header 1 [package=1x01_offset]  # not connected
  JP4 = Header 1 [package=1x01_offset]  # not connected
  JP5 = Header 1 [package=1x01_offset]  # not connected
  JP6 = Header 1 [package=1x01_offset]
  JP7 = Header 1 [package=1x01_offset]
  JP8 = Header 1 [package=1x01_offset]
  JP9 = Header 1 [package=1x01_offset]
  JP10 = Header 1 [package=1x01_offset]
  JP11 = Header 1 [package=1x01_offset]
  JP12 = Header 1 [package=1x01_offset]
  JP13 = Header 1 [package=1x01_offset]
  JP14 = Header 1 [package=1x01_offset]
  JP15 = Header 1 [package=1x01_offset]
  JP16 = Header 1 [package=1x01_offset]
  JP17 = Header 1 [package=1x01_offset]
  JP18 = Header 1 [package=1x01_offset]
  JP19 = Header 1 [package=1x01_offset]
  JP20 = Header 1 [package=1x01_offset]
  JP21 = Header 1 [package=1x01_offset]
  JP22 = Header 1 [package=1x01_offset]
  JP23 = Header 1 [package=1x01_offset]
  JP24 = Header 1 [package=1x01_offset]
  JP25 = Header 1 [package=1x01_offset]
  JP26 = Header 1 [package=1x01_offset]
  JP27 = Header 1 [package=1x01_offset]
  JP28 = Header 1 [package=1x01_offset]
  JP29 = Header 1 [package=1x01_offset]
  JP30 = Header 1 [package=1x01_offset]  # not connected
  JP31 = Header 1 [package=1x01_offset]  # not connected
  JP32 = Header 1 [package=1x01_offset]  # not connected
  JP33 = Header 1 [package=1x01_offset]  # not connected
  JP34 = Header 1 [package=1x01_offset]  # not connected
  JP35 = Header 1 [package=1x01_offset]  # not connected
  JP36 = Header 1 [package=1x01_offset]  # not connected
  JP37 = Header 1 [package=1x01_offset]  # not connected
  JP46 = Header 1 [package=1x01_offset]
  JP47 = Header 1 [package=1x01_offset]
  JP48 = Header 1 [package=1x01_offset]
  JP49 = Header 1 [package=1x01_offset]
  JP50 = Header 1 [package=1x01_offset]
  JP51 = Header 1 [package=1x01_offset]
  JP52 = Header 1 [package=1x01_offset]
  JP53 = Header 1 [package=1x01_offset]
  JP54 = Header 1 [package=1x01_offset]
  JP55 = Header 1 [package=1x01_offset]
  JP56 = Header 1 [package=1x01_offset]
  JP57 = Header 1 [package=1x01_offset]
  JP58 = Header 1 [package=1x01_offset]
  JP59 = Header 1 [package=1x01_offset]
  JP60 = Header 1 [package=1x01_offset]
  JP61 = Header 1 [package=1x01_offset]
  JP62 = Header 1 [package=1x01_offset]  # not connected
  JP63 = Header 1 [package=1x01_offset]
  JP64 = Header 1 [package=1x01_offset]
  JP65 = Header 1 [package=1x01_offset]
  JP66 = Header 1 [package=1x01_offset]
  JP67 = Header 1 [package=1x01_offset]
  JP68 = Header 1 [package=1x01_offset]
  JP69 = Header 1 [package=1x01_offset]
  JP70 = Header 1 [package=1x01_offset]
  JP71 = Header 1 [package=1x01_offset]
  JP72 = Header 1 [package=1x01_offset]
  JP73 = Header 1 [package=1x01_offset]
  JP74 = Header 1 [package=1x01_offset]
  JP76 = Header 1 [package=1x01_offset]
  JP77 = Header 1 [package=1x01_offset]
  JP78 = Header 1 [package=1x01_offset]
  JP79 = Header 1 [package=1x01_offset]
  JP80 = Header 1 [package=1x01_offset]
  JP81 = Header 1 [package=1x01_offset]
  JP84 = Header 1 [package=1x01_offset]
  JP87 = Header 1 [package=1x01_offset]
  JP88 = Header 1 [package=1x01_offset]
  JP97 = Header 1 [package=1x01_offset]  # not connected
  JP98 = Header 1 [package=1x01_offset]  # not connected
  JP99 = Header 1 [package=1x01_offset]  # not connected
  JP100 = Header 1 [package=1x01_offset]  # not connected
  JP101 = Header 1 [package=1x01_offset]  # not connected
  JP102 = Header 1 [package=1x01_offset]  # not connected
  JP103 = Header 1 [package=1x01_offset]  # not connected
  JP104 = Header 1 [package=1x01_offset]  # not connected
  JP105 = Header 1 [package=1x01_offset]  # not connected
  JP106 = Header 1 [package=1x01_offset]  # not connected
  JP107 = Header 1 [package=1x01_offset]  # not connected
  JP108 = Header 1 [package=1x01_offset]  # not connected
  JP109 = Header 1 [package=1x01_offset]  # not connected
  JP110 = Header 1 [package=1x01_offset]  # not connected
  JP111 = Header 1 [package=1x01_offset]
  JP112 = Header 1 [package=1x01_offset]  # not connected
  Part4 = Triple Axis Gyro Breakout ITG-3200
  Piezo_Speaker = mystery part, 2 pins [chip_label=Piezo]
  Piezo_Speaker1 = mystery part, 2 pins [chip_label=Piezo]
  R1 = Trimmer Potentiometer [maximum_resistance=10kΩ package=THT]
  LCD1 = LCD screen
  R2 = Resistor [tolerance=±5% resistance=100 package=THT]
  R3 = Resistor [tolerance=±5% resistance=100 package=THT]
  R4 = Resistor [tolerance=±5% resistance=100 package=THT]
  R5 = Resistor [tolerance=±5% resistance=220 package=THT]

nets:
  GND: Part2.GND, Part2.P$7, Part2.P$8, Part2.P$11#14, Part2.P$12, Part2.1#143, Part2.P$6, Part2.1#152, Part2.1#156, Part2.P$5#157, Part2.P$5#173, Part2.P$1#210, Part2.P$2#211, Part2.P$4#213, Part2.P$5#214, Part2.N$168, Part2.N$260, Part3.GND, JP6.1, JP7.1, JP8.1, JP9.1, JP10.1, JP17.1, JP20.1, JP27.1, JP29.1, JP51.1, JP69.1, JP73.1, JP79.1, Part4.GND, Piezo_Speaker.pin2, Piezo_Speaker1.pin2, R1.leg1, LCD1.VSS, LCD1.R/W, LCD1.LED-, R2.Pin_1, R3.Pin_1, R4.Pin_1
  N1: Part2.AREF, JP46.1
  N2: Part2.D13, JP47.1, LCD1.DB7
  N3: Part2.D12, JP53.1, LCD1.DB6
  N4: Part2.D11, JP52.1, LCD1.DB5
  N5: Part2.D10, JP50.1, LCD1.DB4
  N6: Part2.D9, JP48.1, LCD1.E
  N7: Part2.D8, JP49.1, LCD1.RS
  N8: Part2.D0, Part2.N$169, Part3.TXD, JP57.1, JP77.1
  N9: Part2.D1, Part2.N$170, Part3.RXD, JP56.1, JP78.1
  N10: Part2.D2, JP58.1
  N11: Part2.D3, Part2.1#146, Part2.P$5#147, JP60.1, Piezo_Speaker1.pin1
  N12: Part2.D4, Part2.1#137, Part2.P$5#138, JP61.1, Piezo_Speaker.pin1
  N13: Part2.D5, JP55.1
  N14: Part2.D6, JP59.1
  N15: Part2.D7, JP54.1
  N16: Part2.VIN, JP28.1
  VCC: Part2.+5V, Part2.P$5#190, Part2.P$1#200, Part2.P$2#201, Part2.P$4#203, Part2.P$5#204, Part2.P$5#219, Part2.P$11#225, Part2.P$2#228, Part2.P$10, Part2.N$142, Part3.VCC, JP11.1, JP12.1, JP13.1, JP14.1, JP15.1, JP18.1, JP21.1, JP24.1, JP72.1, JP74.1, JP80.1, Part4.VCC, R1.leg2, LCD1.VDD
  N17: Part2.3.3V, JP26.1
  N18: Part2.RESET, JP25.1
  N19: Part2.A5, JP66.1
  N20: Part2.A4, JP63.1
  N21: Part2.A3, JP65.1
  N22: Part2.A2, JP67.1
  N23: Part2.A1, Part2.P$5#141, JP64.1, JP87.1, Part4.SDA
  N24: Part2.A0, Part2.P$5#131, JP68.1, JP81.1, JP84.1, Part4.SCL
  N25: Part2.P$5#170, JP16.1, JP22.1, JP70.1, JP76.1, Part4.VLOGIC
  N26: Part2.P$5#193, JP88.1, Part4.CLKIN
  N27: Part2.P$5#196, JP19.1, JP23.1, JP71.1, Part4.INT
  N28: Part2.N$72, Part2.N$81, R2.Pin_0, R3.Pin_0, R4.Pin_0, R5.Pin_1
  N29: Part2.N$110, JP111.1, LCD1.V0
  N30: Part2.N$228, R1.wiper
  N31: Part2.N$265, R5.Pin_0

custom parts:
  Adafruit Proto Shield for Arduino Kit - v.5: Arduino prototyping shield designed by Adafruit Industries
