# Fritzing sketch Robot (saved by Fritzing 0.9.1b)
breadboards: 1

parts:
  Part1 = HC-SR04 Ultrasonic Rangemeter
  M1 = DC Motor
  M2 = DC Motor
  LM35_TempSensor1 = LM35 TempSensor
  VCC1 = 4 x AAA Battery Mount
  Part2 = Arduino Uno (Rev3)
  Part3 = 2A MOTOR SHIELD 9
  U1 = SWITCH_SPDT [package=kps-1290]
  Part6 = Bluetooth HC-05 Macho
  RE1 = Rotary Encoder [package=THT]
  Part8 = Arduino Prototyping Shield
  R2 = Resistor [tolerance=±5% resistance=2.0k package=THT]
  R3 = Resistor [tolerance=±5% resistance=1k package=THT]
  RE4 = Rotary Encoder [package=THT]
  JP7 = Header 1 [package=1x01_offset]
  JP12 = Header 1 [package=1x01_offset]
  C1 = Ceramic Capacitor [capacitance=100nF package="100 mil [THT, multilayer]"]
  C2 = Ceramic Capacitor [capacitance=100nF package="100 mil [THT, multilayer]"]
  R4 = Resistor [tolerance=±5% resistance=10k package=THT]
  Part9 = Tri-Axis Gyro Breakout - L3G4200D
  C5 = Tantalum Capacitor [capacitance=1μF package="100 mil [THT, tantalum]"]

nets:
  N1: Part1.Trig, Part8.D8
  N2: Part1.Echo, Part8.A3
  N3: Part1.GND, Part8.N$299
  N4: M1.pin_1, Part3.M1+, C1.1
  N5: M1.pin_2, Part3.M1-, C1.0
  N6: M2.pin_1, Part3.M2+, C2.1
  N7: M2.pin_2, Part3.M2-, C2.0
  N8: LM35_TempSensor1.POWER, Part8.N$332
  N9: LM35_TempSensor1.GND, Part8.A0
  N10: LM35_TempSensor1.INPUT, Part8.N$27
  N11: VCC1.-, Part3.GND#0
  N12: VCC1.+, U1.O
  N13: Part2.A0, Part3.A0
  N14: Part2.A1, Part3.A1
  N15: Part2.A2, Part3.A2
  N16: Part2.A3, Part3.A3
  N17: Part2.A4/SDA, Part3.A4
  N18: Part2.A5/SCL, Part3.A5
  N19: Part2.D8, Part3.D8
  N20: Part2.D9_PWM, Part3.D9
  N21: Part2.D10_PWM/SS, Part3.D10
  N22: Part2.D11_PWM/MOSI, Part3.D11
  N23: Part2.D12/MISO, Part3.D12
  N24: Part2.D13/SCK, Part3.D13
  N25: Part2.GND, Part3.GND#connector1pad-0-1-1-48-61, Part3.GND#connector1pad-0-1-9-9-4-9, Part3.GND#connector1pad-4-5-0-39-8-14
  N26: Part2.AREF, Part3.AFER
  N27: Part2.D1/TX, Part3.D1
  N28: Part2.D2, Part3.D2
  N29: Part2.D3_PWM, Part3.D3
  N30: Part2.D4, Part3.D4
  N31: Part2.D5_PWM, Part3.D5
  N32: Part2.D6_PWM, Part3.D6
  N33: Part2.D7, Part3.D7
  N34: Part2.RESET, Part3.RST
  3V3: Part2.3V3, Part3.3V3
  5V: Part2.5V, Part3.5V
  VIN: Part2.VIN, Part3.VIN
  N35: Part3.D0, U1.P
  N36: Part6.TXD, Part8.D0(RX)
  N37: Part6.RXD, R2.Pin_1, R3.Pin_0
  VCC: Part6.VCC, Part8.N$178, Part8.N$296, Part9.VCC
  N38: Part6.GND, Part8.N$118, R2.Pin_0
  N39: RE1.EncoderPinA, Part8.N$77
  N40: RE1.EncoderPinC, Part8.N$67
  N41: RE1.EncoderPinB, Part8.N$177
  N42: Part8.D1(TX), R3.Pin_1
  N43: Part8.D2, Part8.N$400, JP7.1
  N44: Part8.D11, Part8.N$309, JP12.1
  N45: Part8.A4, Part8.N$282, Part9.SDA
  N46: Part8.A5, Part8.N$295, Part9.SCL
  N47: Part8.N$16, RE4.EncoderPinA
  N48: Part8.N$17, Part8.N$381
  N49: Part8.N$26, C5.+
  N50: Part8.N$37, RE4.EncoderPinB
  N51: Part8.N$41, RE4.EncoderPinC
  N52: Part8.N$76, Part8.N$317, Part9.GND
  N53: Part8.N$273, Part9.INT1
  N54: Part8.N$281, Part9.SDO
  N55: Part8.N$304, C5.-
  N56: Part8.N$312, R4.Pin_0
  N57: Part8.N$314, Part9.INT2
  N58: Part8.N$315, Part9.CS
  N59: Part8.N$410, R4.Pin_1

notes:
  Encoder #2 to help wheels turn at the same rate so the robot goes straight
  Encoder #1 to help wheels turn at the same rate so the robot goes straight
  Gyroscope/Accelerometer used to increase turning precision
  HC-05 Bluetooth for wireless communication between gyroscopic controller and robot
  Prototyping shield is detached from the motor shield to help display wiring
  LM35 Temperature Sensor
